# Fritzing sketch ESP_RFID_Thief (saved by Fritzing 0.9.2b)
breadboards: 1

parts:
  Part1 = Adafruit Feather HUZZAH ESP8266 [part_number="Adafruit #2821"]
  Part2 = Lithium Ion Polymer Battery 3.7v 2000mAh [part_number=2011]  # not connected
  J1 = Screw terminal - 2 pins [package=THT]  # not connected
  J2 = Screw terminal - 2 pins [package=THT]  # not connected
  J3 = Screw terminal - 2 pins [package=THT]  # not connected
  J4 = Screw terminal - 2 pins [package=THT]  # not connected
  J5 = Screw terminal - 2 pins [package=THT]
  J6 = Screw terminal - 2 pins [package=THT]
  J7 = Screw terminal - 2 pins [package=THT]
  J8 = Screw terminal - 2 pins [package=THT]
  BATT1 = 4xAA Switchable Battery Pack w/JST connector
  BATT2 = 4xAA Switchable Battery Pack w/JST connector

nets:
  N1: Part1.GND, J6.pin2, J7.pin1, J7.pin2, BATT1.NEG
  N2: Part1.GPIO5/SCL, J5.pin1
  N3: Part1.GPIO4/SDA, J5.pin2
  N4: J8.pin1, J8.pin2, BATT2.POS
  N5: BATT1.POS, BATT2.NEG

notes:
  TB2 Terminal Block on MaxiProx 5375
  TB2-2 Data1/CLK->White->5
  TB2-1 Data0/Data->Green->4
  TB1 Terminal Block on MaxiProx 5375
  TB1-3 Ground->Black->(-)8xAA Battery Holder
  TB1-1 +DC->Red->(+)8xAA Battery Holder
  Dont forget to shunt pins 1&2 on P2 for 12V
  Two 4xAA Holders Wired in Series
  or you may use an 8xAA Holder or any 12V DC Power Source
  This provides a 12V Power Source for the MaxiProx 5375
  Do not forget to connect the ground to the Adafruit Feather Huzzah as well or you may get invalid data or no data at all
  Adafruit Feather Huzzah ESP8266 12E
  3.7V Lipo Battery, can be more mAH if going for longer runtime
  Attaches to JST connector on ESP
  This is a schematic of the ESP_RFID_Thief by Corey Harding
  This remix adds logging captures to the onboard SPIFFS file system, WiFi access to view the capture logs, and reduces the cost and number of components needed to construct such a device
  Files available at:
  https://github.com/exploitagency/github-ESP_RFID_Thief
  More info on construction and use visit:
  https://www.LegacySecurityGroup.com
  Original Tastic RFID Thief is by Bishop Fox

custom parts:
  Adafruit Feather HUZZAH ESP8266: his is the Adafruit Feather HUZZAH ESP8266 - our take on an 'all-in-one' ESP8266 WiFi development board with built in USB and battery charging. Its an ESP8266 WiFi module with all the extras you need, ready to rock! We have other boards in the Feather family, check'em out here. At the Feather HUZZAH's heart is an ESP8266 WiFi microcontroller clocked at 80 MHz and at 3.3V logic. This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
  Lithium Ion Polymer Battery 3.7v 2000mAh: Lithium ion polymer (also known as 'lipo' or 'lipoly') batteries are thin, light and powerful. The output ranges from 4.2V when completely charged to 3.7V. This battery has a capacity of 2000mAh. The batteries come pre-attached with a genuine 2-pin JST-PH connector as shown and include the necessary protection circuitry.
  4xAA Switchable Battery Pack w/JST connector: 4xAA Switchable Battery Pack with JST connector
